# Fritzing sketch receiver_fritzing (saved by Fritzing 0.9.3b)

parts:
  Parça1 = Arduino Uno (Rev3)
  Parça2 = NRF24L01+ Breakout Board

nets:
  N1: Parça1.D8, Parça2.IRQ
  N2: Parça1.D9_PWM, Parça2.CE
  N3: Parça1.D10_PWM/SS, Parça2.CS
  N4: Parça1.D11_PWM/MOSI, Parça2.MOSI
  N5: Parça1.D12/MISO, Parça2.MISO
  N6: Parça1.D13/SCK, Parça2.SCK
  5V: Parça1.5V, Parça2.VCC
  GND: Parça1.GND, Parça2.GND
