# Fritzing sketch transmitter_fritzing (saved by Fritzing 0.9.3b)
breadboards: 1

parts:
  Parça3 = Arduino Uno (Rev3)
  Parça4 = NRF24L01+ Breakout Board
  S1 = Round Pushbutton
  S2 = Round Pushbutton
  S3 = Round Pushbutton
  S4 = Round Pushbutton
  S5 = Round Pushbutton
  R1 = Resistor [tolerance=±5% resistance=220 package="0402 [SMD]"]
  R3 = Resistor [tolerance=±5% resistance=220 package="0402 [SMD]"]
  R4 = Resistor [tolerance=±5% resistance=220 package="0402 [SMD]"]
  R5 = Resistor [tolerance=±5% resistance=220 package="0402 [SMD]"]
  R6 = Resistor [tolerance=±5% resistance=220 package="0402 [SMD]"]
  R7 = Rotary Potentiometer (Small) [maximum_resistance=100kΩ package=THT]
  R8 = Rotary Potentiometer (Small) [maximum_resistance=100kΩ package=THT]
  R9 = Rotary Potentiometer (Small) [maximum_resistance=100kΩ package=THT]
  R10 = Rotary Potentiometer (Small) [maximum_resistance=100kΩ package=THT]
  Parça5 = Thumb Joystick

nets:
  N1: Parça3.A0, R7.wiper
  N2: Parça3.A1, R8.wiper
  N3: Parça3.A2, R9.wiper
  N4: Parça3.A3, R10.wiper
  N5: Parça3.A4/SDA, Parça5.HORZ
  N6: Parça3.A5/SCL, Parça5.VERT
  N7: Parça3.D8, Parça4.IRQ
  N8: Parça3.D9_PWM, Parça4.CE
  N9: Parça3.D10_PWM/SS, Parça4.CS
  N10: Parça3.D11_PWM/MOSI, Parça4.MOSI
  N11: Parça3.D12/MISO, Parça4.MISO
  N12: Parça3.D13/SCK, Parça4.SCK
  N13: Parça3.D2, S5.leg0, R5.Pin_0
  N14: Parça3.D3_PWM, S4.leg0, R4.Pin_0
  N15: Parça3.D4, S3.leg0, R3.Pin_0
  N16: Parça3.D5_PWM, S2.leg0, R6.Pin_0
  VCC: Parça3.5V, Parça4.VCC, S1.leg1, S2.leg1, S3.leg1, S4.leg1, S5.leg1, R7.leg2, R8.leg2, R9.leg2, R10.leg2, Parça5.VCC
  GND: Parça3.GND, Parça4.GND, R1.Pin_1, R3.Pin_1, R4.Pin_1, R5.Pin_1, R6.Pin_1, R7.leg1, R8.leg1, R9.leg1, R10.leg1, Parça5.GND
  N17: S1.leg0, R1.Pin_0
